# Fritzing sketch LedsMaze (saved by Fritzing 0.9.3b)
breadboards: 1

parts:
  Composant4 = Arduino Nano (Rev3.0)
  Composant5 = 9 Degrees of Freedom - Sensor Stick

nets:
  N1: Composant4.5V, Composant5.SCL
  N2: Composant4.A5, Composant5.GND
  N3: Composant4.A4, Composant5.VCC

notes:
  GY-521
